# Fritzing sketch neopellet-pcb (saved by Fritzing 0.9.10b)
circuit board: 7cm x 10cm
breadboards: 1

parts:
  OLED1 = OLED 128x64 I2C Monochrome Display
  ExtruderMotor = female pin header, 8 pins [form="♀ (female)"]
  fan = female pin header, 3 pins [form="♀ (female)"]
  tempOut = female pin header, 3 pins [form="♀ (female)"]
  temp = KY-040 Rotary encoder [package=THT]
  M1 = DOIT Esp32 DevKit v1 (30 pins long, 11 pins width) [part_number=ESP32S-PIN30]
  fan_2 = KY-040 Rotary encoder [package=THT]
  RE3 = KY-040 Rotary encoder [package=THT]
  robot = female pin header, 3 pins [form="♀ (female)"]
  Part1 = Adafruit Thermocouple Amplifier MAX31855 [part_number="Adafruit #269"]
  jumper = female pin header, 1 pin [form="♀ (female)"]
  jumper1 = female pin header, 1 pin [form="♀ (female)"]
  jumper2 = female pin header, 1 pin [form="♀ (female)"]
  jumper3 = female pin header, 1 pin [form="♀ (female)"]
  robot1 = female pin header, 4 pins [form="♀ (female)"]
  jumper6 = female alternating pin header, 1 pin [form="♀ (female)"]  # not connected
  jumper5 = rounded female pin header, 1 pin [form="♀ (female rounded)"]  # not connected
  jumper4 = female pin header, 1 pin [form="♀ (female)"]  # not connected
  jumper7 = female pin header, 1 pin [form="♀ (female)"]  # not connected

nets:
  GND: OLED1.GND, ExtruderMotor.pin1, ExtruderMotor.pin2, ExtruderMotor.pin3, fan.pin2, tempOut.pin2, temp.GND, M1.GND, fan_2.GND, RE3.GND, robot.pin2, Part1.GND, jumper.pin1, jumper1.pin1, jumper2.pin1, jumper3.pin1, robot1.pin4
  VCC: OLED1.VDD, fan.pin1, tempOut.pin1, temp.Vcc, M1.VIN, fan_2.Vcc, RE3.Vcc, robot.pin1, Part1.VIN, robot1.pin3
  N1: OLED1.SCK, M1.D21, robot1.pin2
  N2: OLED1.SDA, M1.D22, robot1.pin1
  N3: ExtruderMotor.pin5, M1.D27
  N4: ExtruderMotor.pin6, M1.D26
  N5: ExtruderMotor.pin7, M1.D25
  N6: fan.pin3, M1.D13
  N7: tempOut.pin3, M1.D12
  N8: temp.SW, M1.D18
  N9: temp.DT, M1.D19
  N10: temp.CLK, M1.RX0
  N11: M1.D15, fan_2.SW
  N12: M1.D2, fan_2.DT
  N13: M1.D4, fan_2.CLK
  N14: M1.RX2, RE3.SW
  N15: M1.TX2, RE3.DT
  N16: M1.D5, RE3.CLK
  N17: M1.D35, Part1.CLK
  N18: M1.D32, Part1.CS
  N19: M1.D33, Part1.DO
  N20: M1.D14, robot.pin3

custom parts:
  KY-040 Rotary encoder: KY-040 Rotary Encoder with switch on breakout borad from AZ Delivery
  DOIT Esp32 DevKit v1 (30 pins long, 11 pins width): The DOIT Esp32 DevKit v1 is one of the development board created by DOIT to evaluate the ESP-WROOM-32 module. It is based on the ESP32 microcontroller that boasts Wifi, Bluetooth, Ethernet and Low Power support all in a single chip. (vanepp) made breadboard work, adjusted pin numbering and labels and reduced size of schematic and cleaned up pcb. This chip is 30pins long (2 x15) and 11 pins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
  Adafruit Thermocouple Amplifier MAX31855: Thermocouples are very sensitive, requiring a good amplifier with a cold-compensation reference. The MAX31855K does everything for you, and can be easily interfaced with any microcontroller, even one without an analog input. This breakout board has the chip itself, a 3.3V regulator with 10uF bypass capacitors and level shifting circuitry, all assembled and tested. Comes with a 2 pin terminal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
